// Logisim project test.circ as structural Verilog: 1 circuit, main circuit main
module main (
  output out_1,
  output out_2,
  output out_3
);

  wire clock_1_out, d_ff_2_qn, nand_1_out, nand_2_out, nand_3_out, nor_1_out, nor_2_out, not_1_out;

  Clock clock_1 (.out(clock_1_out));
  D_Flip_Flop d_ff_1 (.clk(clock_1_out), .D(nor_1_out), .Q(out_1));  // open: Qn, preset, en, reset
  nor nor_1 (nor_1_out, out_1, out_3);
  D_Flip_Flop d_ff_2 (.clk(clock_1_out), .D(not_1_out), .Q(out_2), .Qn(d_ff_2_qn));  // open: preset, en, reset
  not not_1 (not_1_out, nor_2_out);
  nor nor_2 (nor_2_out, d_ff_2_qn, out_1);
  nand nand_1 (nand_1_out, nor_1_out, out_2);
  nand nand_2 (nand_2_out, d_ff_2_qn, out_3);
  nand nand_3 (nand_3_out, nand_1_out, nand_2_out);
  D_Flip_Flop d_ff_3 (.clk(clock_1_out), .D(nand_3_out), .Q(out_3));  // open: Qn, preset, en, reset
endmodule
