// Logisim project circ.circ as structural Verilog: 1 circuit, main circuit main
module main (
  output out_1,
  output out_2,
  output out_3
);

  wire clock_1_out, j_k_ff_1_qn, j_k_ff_3_qn, nand_1_out, nand_2_out, nand_3_out, not_1_out, not_2_out;

  Clock clock_1 (.out(clock_1_out));
  J_K_Flip_Flop j_k_ff_1 (
    .J(out_2), .clk(clock_1_out), .K(nand_3_out), .Q(out_1), .Qn(j_k_ff_1_qn));  // open: preset, en, reset
  nand nand_1 (nand_1_out, out_1, j_k_ff_3_qn);
  J_K_Flip_Flop j_k_ff_2 (.J(j_k_ff_1_qn), .clk(clock_1_out), .K(not_1_out), .Q(out_2));  // open: Qn, preset, en, reset
  not not_1 (not_1_out, nand_1_out);
  not not_2 (not_2_out, nand_2_out);
  nand nand_2 (nand_2_out, j_k_ff_1_qn, out_2);
  nand nand_3 (nand_3_out, out_2, j_k_ff_3_qn);
  J_K_Flip_Flop j_k_ff_3 (
    .J(not_2_out), .clk(clock_1_out), .K(j_k_ff_1_qn), .Q(out_3), .Qn(j_k_ff_3_qn));  // open: preset, en, reset
endmodule
